// Logisim project lab1.circ as structural Verilog
module One_bit_comparator (
  input  A,
  input  B,
  output A___B,
  output A___B_2,
  output A___B_3
);

  wire and_2_out, and_3_out, not_1_out, not_2_out;

  not not_1 (not_1_out, A);
  not not_2 (not_2_out, B);
  and and_1 (A___B, not_2_out, A);
  and and_2 (and_2_out, A, B);
  and and_3 (and_3_out, not_2_out, not_1_out);
  and and_4 (A___B_3, not_1_out, B);
  or or_1 (A___B_2, and_2_out, and_3_out);

  // Notes on the sheet:
  //   A'
  //   B'
  //   AB'
  //   A'B
  //   AB+A'B'
endmodule

module Dos_bit_comparator (
  input  A0,
  input  A1,
  input  B0,
  input  B1,
  output A_B,
  output A_B_2,
  output A_B_3
);

  wire and_1_out, and_2_out, and_3_out, and_4_out, and_5_out, and_6_out, and_7_out, and_8_out, and_9_out,
       and_10_out, not_1_out, not_2_out, not_3_out, not_4_out;

  not not_1 (not_1_out, A0);
  not not_2 (not_2_out, A1);
  not not_3 (not_3_out, B0);
  not not_4 (not_4_out, B1);
  and and_1 (and_1_out, A0, not_3_out, not_4_out);
  and and_2 (and_2_out, A0, not_3_out, B1);
  and and_3 (and_3_out, A1, not_4_out);
  and and_4 (and_4_out, not_1_out, not_2_out, not_3_out, not_4_out);
  and and_5 (and_5_out, not_1_out, A1, not_3_out, B1);
  and and_6 (and_6_out, A0, not_2_out, B0, not_4_out);
  and and_7 (and_7_out, A0, A1, B0, B1);
  and and_8 (and_8_out, not_2_out, B0, B1);
  and and_9 (and_9_out, not_1_out, A1, B0);
  and and_10 (and_10_out, not_1_out, not_2_out);
  or or_1 (A_B, and_1_out, and_2_out, and_3_out);
  or or_2 (A_B_2, and_4_out, and_5_out, and_6_out, and_7_out);
  or or_3 (A_B_3, and_8_out, and_9_out, and_10_out);
endmodule
