// Logisim project laborat1.circ as structural Verilog: 9 circuits, main circuit main
module main (
);

  Sorting_network sorting_network_1 ();  // open: s_4, s_3, s_2, s_1, s, i_7, i_6, i_5, i_4, i_3, i_2, i_1, i, s_5, s_6, s_7
  Sorting_network sorting_network_2 ();  // open: s_4, s_3, s_2, s_1, s, i_7, i_6, i_5, i_4, i_3, i_2, i_1, i, s_5, s_6, s_7
endmodule

module Un_bit_comparador (
  input  A,
  input  B,
  input  E,
  input  N,
  output S,
  output I
);

  wire and_1_out, and_2_out, and_3_out, and_4_out, and_5_out, and_6_out, not_1_out, not_2_out, not_3_out,
       not_4_out;

  not not_1 (not_1_out, A);
  not not_2 (not_2_out, B);
  not not_3 (not_3_out, E);
  not not_4 (not_4_out, N);
  and and_1 (and_1_out, not_2_out, E);
  and and_2 (and_2_out, A, not_2_out);
  and and_3 (and_3_out, A, E);
  and and_4 (and_4_out, not_1_out, B);
  and and_5 (and_5_out, not_1_out, N);
  and and_6 (and_6_out, B, N);
  or or_1 (S, and_1_out, and_2_out, and_3_out);
  or or_2 (I, and_4_out, and_5_out, and_6_out);
endmodule

module Eight_bit_comparator (
  input  B7,
  input  A7,
  input  A6,
  input  B6,
  input  A5,
  input  B5,
  input  A4,
  input  B4,
  input  A3,
  input  B3,
  input  A2,
  input  B2,
  input  A1,
  input  B1,
  input  A0,
  input  B0,
  output out_17,
  output out_18
);

  wire un_bit_comparador_1_i, un_bit_comparador_1_s, un_bit_comparador_2_i, un_bit_comparador_2_s,
       un_bit_comparador_3_i, un_bit_comparador_3_s, un_bit_comparador_4_i, un_bit_comparador_4_s,
       un_bit_comparador_5_i, un_bit_comparador_5_s, un_bit_comparador_6_i, un_bit_comparador_6_s,
       un_bit_comparador_7_i, un_bit_comparador_7_s;

  Un_bit_comparador un_bit_comparador_1 (
    .A(A0), .B(B0), .S(un_bit_comparador_1_s), .I(un_bit_comparador_1_i));  // open: E, N
  Un_bit_comparador un_bit_comparador_2 (
    .A(A1), .B(B1), .E(un_bit_comparador_1_s), .N(un_bit_comparador_1_i), .S(un_bit_comparador_2_s),
    .I(un_bit_comparador_2_i));
  Un_bit_comparador un_bit_comparador_3 (
    .A(A2), .B(B2), .E(un_bit_comparador_2_s), .N(un_bit_comparador_2_i), .S(un_bit_comparador_3_s),
    .I(un_bit_comparador_3_i));
  Un_bit_comparador un_bit_comparador_4 (
    .A(A3), .B(B3), .E(un_bit_comparador_3_s), .N(un_bit_comparador_3_i), .S(un_bit_comparador_4_s),
    .I(un_bit_comparador_4_i));
  Un_bit_comparador un_bit_comparador_5 (
    .A(A4), .B(B4), .E(un_bit_comparador_4_s), .N(un_bit_comparador_4_i), .S(un_bit_comparador_5_s),
    .I(un_bit_comparador_5_i));
  Un_bit_comparador un_bit_comparador_6 (
    .A(A5), .B(B5), .E(un_bit_comparador_5_s), .N(un_bit_comparador_5_i), .S(un_bit_comparador_6_s),
    .I(un_bit_comparador_6_i));
  Un_bit_comparador un_bit_comparador_7 (
    .A(A6), .B(B6), .E(un_bit_comparador_6_s), .N(un_bit_comparador_6_i), .S(un_bit_comparador_7_s),
    .I(un_bit_comparador_7_i));
  Un_bit_comparador un_bit_comparador_8 (
    .A(B7), .B(A7), .E(un_bit_comparador_7_s), .N(un_bit_comparador_7_i), .S(out_17), .I(out_18));
endmodule

module Eight_bit_comparator_Test (
  input  in_1,
  input  in_2,
  input  in_3,
  input  A,
  input  in_5,
  input  in_6,
  input  in_7,
  input  in_8,
  input  in_9,
  input  in_10,
  input  in_11,
  input  B,
  input  in_13,
  input  in_14,
  input  in_15,
  input  in_16,
  output out_17,
  output out_18
);

  Eight_bit_comparator eight_bit_comparator_1 (
    .B7(in_8), .A7(in_16), .A6(in_7), .B6(in_15), .A5(in_6), .B5(in_14), .A4(in_5), .B4(in_13), .A3(A),
    .B3(B), .A2(in_3), .B2(in_11), .A1(in_2), .B1(in_10), .A0(in_1), .B0(in_9), .out_17(out_17),
    .out_18(out_18));

  // Notes on the sheet:
  //   0|1=> A<B
  //   1|0=> A>B
  //   0|0=> A=B
endmodule

module One_wire_sorting_network (
  input  [7:0] A,
  input  [7:0] B,
  output [7:0] Smaller,
  output [7:0] Greater
);

  wire [1:0] eight_bit_comparator_1_out_18;

  Eight_bit_comparator eight_bit_comparator_1 (
    .B7(B[7]), .A7(A[7]), .A6(A[6]), .B6(B[6]), .A5(A[5]), .B5(B[5]), .A4(A[4]), .B4(B[4]), .A3(A[3]),
    .B3(B[3]), .A2(A[2]), .B2(B[2]), .A1(A[1]), .B1(B[1]), .A0(A[0]), .B0(B[0]),
    .out_17(eight_bit_comparator_1_out_18[1]), .out_18(eight_bit_comparator_1_out_18[0]));
  Multiplexer #(.select(2), .width(8), .enable("false")) multiplexer_1 (
    .in0(A), .in1(B), .in2(A), .out(Greater), .sel(eight_bit_comparator_1_out_18));  // open: in3
  Multiplexer #(.select(2), .width(8), .enable("false")) multiplexer_2 (
    .in0(A), .in1(A), .in2(B), .out(Smaller), .sel(eight_bit_comparator_1_out_18));  // open: in3
endmodule

module Sorting_network (
  input  [7:0] i,
  input  [7:0] i_1,
  input  [7:0] i_2,
  input  [7:0] i_3,
  input  [7:0] i_4,
  input  [7:0] i_5,
  input  [7:0] i_6,
  input  [7:0] i_7,
  output [7:0] s,
  output [7:0] s_1,
  output [7:0] s_2,
  output [7:0] s_3,
  output [7:0] s_4,
  output [7:0] s_5,
  output [7:0] s_6,
  output [7:0] s_7
);

  wire [7:0] four_sorting_network_1_cero, four_sorting_network_1_one, four_sorting_network_1_three,
       four_sorting_network_1_two, four_sorting_network_2_cero, four_sorting_network_2_one,
       four_sorting_network_2_three, four_sorting_network_2_two, split_largerhalf_smallerhalf_1_out_9,
       split_largerhalf_smallerhalf_1_out_10, split_largerhalf_smallerhalf_1_out_11,
       split_largerhalf_smallerhalf_1_out_12, split_largerhalf_smallerhalf_1_out_13,
       split_largerhalf_smallerhalf_1_out_14, split_largerhalf_smallerhalf_1_out_15,
       split_largerhalf_smallerhalf_1_out_16;

  Four_Sorting_network four_sorting_network_1 (
    .in_1(i), .in_2(i_1), .in_3(i_2), .in_4(i_3), .Cero(four_sorting_network_1_cero),
    .One(four_sorting_network_1_one), .Two(four_sorting_network_1_two), .Three(four_sorting_network_1_three));
  Four_Sorting_network four_sorting_network_2 (
    .in_1(i_4), .in_2(i_5), .in_3(i_6), .in_4(i_7), .Cero(four_sorting_network_2_cero),
    .One(four_sorting_network_2_one), .Two(four_sorting_network_2_two), .Three(four_sorting_network_2_three));
  Split_largerHalf_smallerHalf split_largerhalf_smallerhalf_1 (
    .in_1(four_sorting_network_1_cero), .in_2(four_sorting_network_1_one), .in_3(four_sorting_network_1_two),
    .in_4(four_sorting_network_1_three), .in_5(four_sorting_network_2_cero),
    .in_6(four_sorting_network_2_one), .in_7(four_sorting_network_2_two),
    .in_8(four_sorting_network_2_three), .out_9(split_largerhalf_smallerhalf_1_out_9),
    .out_10(split_largerhalf_smallerhalf_1_out_10), .out_11(split_largerhalf_smallerhalf_1_out_11),
    .out_12(split_largerhalf_smallerhalf_1_out_12), .out_13(split_largerhalf_smallerhalf_1_out_13),
    .out_14(split_largerhalf_smallerhalf_1_out_14), .out_15(split_largerhalf_smallerhalf_1_out_15),
    .out_16(split_largerhalf_smallerhalf_1_out_16));
  LastOne lastone_1 (
    .in_1(split_largerhalf_smallerhalf_1_out_9), .in_2(split_largerhalf_smallerhalf_1_out_10),
    .in_3(split_largerhalf_smallerhalf_1_out_11), .in_4(split_largerhalf_smallerhalf_1_out_12), .Cero(s),
    .One(s_1), .Two(s_2), .Three(s_3));
  LastOne lastone_2 (
    .in_1(split_largerhalf_smallerhalf_1_out_13), .in_2(split_largerhalf_smallerhalf_1_out_14),
    .in_3(split_largerhalf_smallerhalf_1_out_15), .in_4(split_largerhalf_smallerhalf_1_out_16), .Cero(s_4),
    .One(s_5), .Two(s_6), .Three(s_7));
endmodule

module Four_Sorting_network (
  input  [7:0] in_1,
  input  [7:0] in_2,
  input  [7:0] in_3,
  input  [7:0] in_4,
  output [7:0] Cero,
  output [7:0] One,
  output [7:0] Two,
  output [7:0] Three
);

  wire [7:0] one_wire_sorting_network_1_greater, one_wire_sorting_network_1_smaller,
       one_wire_sorting_network_2_greater, one_wire_sorting_network_2_smaller,
       one_wire_sorting_network_3_greater, one_wire_sorting_network_3_smaller,
       one_wire_sorting_network_4_greater, one_wire_sorting_network_4_smaller;

  One_wire_sorting_network one_wire_sorting_network_1 (
    .A(in_1), .B(in_2), .Smaller(one_wire_sorting_network_1_smaller),
    .Greater(one_wire_sorting_network_1_greater));
  One_wire_sorting_network one_wire_sorting_network_2 (
    .A(in_3), .B(in_4), .Smaller(one_wire_sorting_network_2_smaller),
    .Greater(one_wire_sorting_network_2_greater));
  One_wire_sorting_network one_wire_sorting_network_3 (
    .A(one_wire_sorting_network_1_greater), .B(one_wire_sorting_network_2_smaller),
    .Smaller(one_wire_sorting_network_3_smaller), .Greater(one_wire_sorting_network_3_greater));
  One_wire_sorting_network one_wire_sorting_network_4 (
    .A(one_wire_sorting_network_1_smaller), .B(one_wire_sorting_network_2_greater),
    .Smaller(one_wire_sorting_network_4_smaller), .Greater(one_wire_sorting_network_4_greater));
  One_wire_sorting_network one_wire_sorting_network_5 (
    .A(one_wire_sorting_network_4_smaller), .B(one_wire_sorting_network_3_smaller), .Smaller(Cero),
    .Greater(One));
  One_wire_sorting_network one_wire_sorting_network_6 (
    .A(one_wire_sorting_network_3_greater), .B(one_wire_sorting_network_4_greater), .Smaller(Two),
    .Greater(Three));
endmodule

module Split_largerHalf_smallerHalf (
  input  [7:0] in_1,
  input  [7:0] in_2,
  input  [7:0] in_3,
  input  [7:0] in_4,
  input  [7:0] in_5,
  input  [7:0] in_6,
  input  [7:0] in_7,
  input  [7:0] in_8,
  output [7:0] out_9,
  output [7:0] out_10,
  output [7:0] out_11,
  output [7:0] out_12,
  output [7:0] out_13,
  output [7:0] out_14,
  output [7:0] out_15,
  output [7:0] out_16
);

  One_wire_sorting_network one_wire_sorting_network_1 (.A(in_1), .B(in_8), .Smaller(out_9), .Greater(out_16));
  One_wire_sorting_network one_wire_sorting_network_2 (.A(in_2), .B(in_7), .Smaller(out_10), .Greater(out_15));
  One_wire_sorting_network one_wire_sorting_network_3 (.A(in_3), .B(in_6), .Smaller(out_11), .Greater(out_14));
  One_wire_sorting_network one_wire_sorting_network_4 (.A(in_4), .B(in_5), .Smaller(out_12), .Greater(out_13));
endmodule

module LastOne (
  input  [7:0] in_1,
  input  [7:0] in_2,
  input  [7:0] in_3,
  input  [7:0] in_4,
  output [7:0] Cero,
  output [7:0] One,
  output [7:0] Two,
  output [7:0] Three
);

  wire [7:0] one_wire_sorting_network_1_greater, one_wire_sorting_network_1_smaller,
       one_wire_sorting_network_2_greater, one_wire_sorting_network_2_smaller;

  One_wire_sorting_network one_wire_sorting_network_1 (
    .A(in_2), .B(in_4), .Smaller(one_wire_sorting_network_1_smaller),
    .Greater(one_wire_sorting_network_1_greater));
  One_wire_sorting_network one_wire_sorting_network_2 (
    .A(in_1), .B(in_3), .Smaller(one_wire_sorting_network_2_smaller),
    .Greater(one_wire_sorting_network_2_greater));
  One_wire_sorting_network one_wire_sorting_network_3 (
    .A(one_wire_sorting_network_2_greater), .B(one_wire_sorting_network_1_greater), .Smaller(Two),
    .Greater(Three));
  One_wire_sorting_network one_wire_sorting_network_4 (
    .A(one_wire_sorting_network_2_smaller), .B(one_wire_sorting_network_1_smaller), .Smaller(Cero),
    .Greater(One));
endmodule
