// Logisim project fsm_merging.circ as structural Verilog: 1 circuit, main circuit main
module main (
  input  X,
  output Z1,
  output Z2
);

  wire and_4_out, and_5_out, and_6_out, CLK, CLR, D0, D1, D2, Q0, Q0neg, Q1, Q2;

  Clock u_CLK (.out(CLK));
  Button u_CLR (.out(CLR));
  D_Flip_Flop FF2 (.D(D2), .clk(CLK), .Q(Q2), .reset(CLR));  // open: Qn, preset
  D_Flip_Flop FF1 (.D(D1), .clk(CLK), .Q(Q1), .reset(CLR));  // open: Qn, preset
  D_Flip_Flop FF0 (.D(D0), .clk(CLK), .Q(Q0), .Qn(Q0neg), .reset(CLR));  // open: preset
  not not_1 (D0, X);
  and and_1 (D2, Q0neg, X);
  and and_2 (Z1, Q1, Q0neg);
  and and_3 (Z2, Q1, Q0);
  and and_4 (and_4_out, Q0, X);
  and and_5 (and_5_out, Q1, Q0neg, D0);
  and and_6 (and_6_out, Q2, D0);
  or or_1 (D1, and_4_out, and_5_out, and_6_out);

  // Other names for the same wires on the sheet: Xneg = D0
endmodule
