// Logisim project lab1.circ as structural Verilog
module One_bit_comparator (
  input  in_1,
  input  in_2
);

  wire not_1_out;

  not not_1 (not_1_out, in_2);
endmodule
