// Logisim project lab4 .circ as structural Verilog: 18 circuits, main circuit main
module main (
);

  wire ALUSrc, and_2_out, Branch, CLK, clock_1_out, jr, jump, link, MemRead, MemtoReg, MemWrite, Regdst,
       RegWrite, Reset, Zero;
  wire [1:0] ALUOp;
  wire [2:0] ALU_Oper;
  wire [4:0] multiplexer_1_out, rd, rs, rt, write_reg;
  wire [5:0] funct, Opcode;
  wire [15:0] address;
  wire [25:0] add_26, shifter_1_out;
  wire [27:0] bit_extender_1_out;
  wire [31:0] adder_2_out, AddrPlus4, ALU_result, data_memory_1_read_data, instruction_memory_1_instr,
       multiplexer_4_out, multiplexer_5_out, MUX_B, NextAddr, pc_1_out_addr, RD1, RD2, shifter_2_out, SigEx,
       WriteData;

  Clock clock_1 (.out(clock_1_out));
  Button button_1 (.out(Reset));
  and and_1 (CLK, clock_1_out, ~Zero);  // AND_Gate
  PC pc_1 (.Addr(NextAddr), .CLK(CLK), .RESET(Reset), .Out_Addr(pc_1_out_addr));
  Adder #(.width(32)) adder_1 (.a(32'h4), .b(pc_1_out_addr), .out(AddrPlus4));  // open: cin, cout
  Decoder_jr decoder_jr_1 (.in_1(ALUOp), .in_2(funct), .jr(jr));
  Instruction_memory instruction_memory_1 (.Addr(pc_1_out_addr), .Instr(instruction_memory_1_instr));
  InstDecoder instdecoder_1 (
    .in_1(instruction_memory_1_instr), .OpCode(Opcode), .rs(rs), .rt(rt), .rd(rd), .funct(funct),
    .address(address), .add_26(add_26));
  Multiplexer #(.width(5), .enable("false")) multiplexer_1 (.in0(rt), .in1(rd), .out(multiplexer_1_out), .sel(Regdst));
  Shifter #(.width(26)) shifter_1 (.in(add_26), .\dist (5'b00010), .out(shifter_1_out));
  Multiplexer #(.width(5), .enable("false")) multiplexer_2 (
    .in0(multiplexer_1_out), .in1({5{1'b1}}), .out(write_reg), .sel(link));
  assign bit_extender_1_out = {{2{shifter_1_out[25]}}, shifter_1_out};  // Bit_Extender bit_extender_1
  MAIN_CONTROL main_control_1 (
    .OpCode(Opcode), .Regdst(Regdst), .ALUSrc(ALUSrc), .MemtoReg(MemtoReg), .RegWrite(RegWrite),
    .MemRead(MemRead), .MemWrite(MemWrite), .Branch(Branch), .ALUOp(ALUOp), .jump(jump), .link(link));
  assign SigEx = {{16{address[15]}}, address};  // Bit_Extender bit_extender_2
  Reg_File reg_file_1 (
    .CLK(CLK), .Reset(Reset), .Write_Data(WriteData), .Read_Reg_1(rs), .Read_Reg_2(rt), .Reg_Write(RegWrite),
    .Write_Reg(write_reg), .RD1(RD1), .RD2(RD2));
  Multiplexer #(.width(32), .enable("false")) multiplexer_3 (.in0(RD2), .in1(SigEx), .out(MUX_B), .sel(ALUSrc));
  Shifter #(.width(32)) shifter_2 (.in(SigEx), .\dist (5'b00010), .out(shifter_2_out));
  Adder #(.width(32)) adder_2 (.a(AddrPlus4), .b(shifter_2_out), .out(adder_2_out));  // open: cin, cout
  ALU_Control alu_control_1 (.ALUOp(ALUOp), .func(funct), .ALU_Oper(ALU_Oper));
  and and_2 (and_2_out, Branch, Zero);
  Multiplexer #(.width(32), .enable("false")) multiplexer_4 (
    .in0(AddrPlus4), .in1(adder_2_out), .out(multiplexer_4_out), .sel(and_2_out));
  Multiplexer #(.width(32), .enable("false")) multiplexer_5 (
    .in0(multiplexer_4_out), .in1({AddrPlus4[31:28], bit_extender_1_out}), .out(multiplexer_5_out), .sel(jump));
  ALU_32bit alu_32bit_1 (.ALU_Op(ALU_Oper), .b(MUX_B), .a(RD1), .ALU_Result(ALU_result), .Zero(Zero));
  Multiplexer #(.width(32), .enable("false")) multiplexer_6 (
    .in0(multiplexer_5_out), .in1(RD1), .out(NextAddr), .sel(jr));
  Data_memory data_memory_1 (
    .Address(ALU_result), .Write_data(RD2), .MemRead(MemRead), .MemWrite(MemWrite), .Clk(CLK),
    .Read_data(data_memory_1_read_data));
  Multiplexer #(.width(32), .enable("false")) multiplexer_7 (
    .in0(data_memory_1_read_data), .in1(ALU_result), .out(WriteData), .sel(MemtoReg));
endmodule

module ALU_1bit (
  input  Cin,
  input  A,
  input  B,
  input  [2:0] ALU_Opt,
  input  Ainv,
  input  Binv,
  input  SLT,
  output Result,
  output Cout,
  output Sign
);

  wire A_neg, Aop, B_neg, Bop, overflow_1_r, r_and, r_or, r_sum;
  wire [1:0] decoder_alu_1_out_4;

  not not_1 (A_neg, A);
  not not_2 (B_neg, B);
  Multiplexer #(.enable("false")) multiplexer_1 (.in0(A), .in1(A_neg), .out(Aop), .sel(Ainv));
  Multiplexer #(.enable("false")) multiplexer_2 (.in0(B), .in1(B_neg), .out(Bop), .sel(Binv));
  OverFlow overflow_1 (.A(Cin), .B(Cout), .R(overflow_1_r));
  or or_1 (r_or, Aop, Bop);
  and and_1 (r_and, Aop, Bop);
  FA_1bit fa_1bit_1 (.A(Aop), .B(Bop), .Cin(Cin), .Sum(r_sum), .Cout(Cout));
  SignCalculator signcalculator_1 (.A(r_sum), .B(Cout), .Overflow(overflow_1_r), .sgn(Sign));
  Multiplexer #(.select(2), .enable("false")) multiplexer_3 (
    .in0(r_and), .in1(r_or), .in2(r_sum), .in3(SLT), .out(Result), .sel(decoder_alu_1_out_4));
  Decoder_ALU decoder_alu_1 (.in_1(ALU_Opt[2]), .in_2(ALU_Opt[1]), .in_3(ALU_Opt[0]), .out_4(decoder_alu_1_out_4));

  // Other names for the same wires on the sheet: r_slt = SLT
endmodule

module FA_1bit (
  input  A,
  input  B,
  input  Cin,
  output Sum,
  output Cout
);

  wire and_1_out, and_2_out, and_3_out, and_4_out, and_5_out, and_6_out, and_7_out, not_1_out, not_2_out,
       not_3_out, not_4_out, not_5_out, not_6_out;

  not not_1 (not_1_out, A);
  not not_2 (not_2_out, B);
  not not_3 (not_3_out, A);
  not not_4 (not_4_out, Cin);
  not not_5 (not_5_out, B);
  not not_6 (not_6_out, Cin);
  and and_1 (and_1_out, B, Cin);
  and and_2 (and_2_out, A, Cin);
  and and_3 (and_3_out, A, B);
  and and_4 (and_4_out, not_1_out, not_2_out, Cin);
  and and_5 (and_5_out, not_3_out, B, not_4_out);
  and and_6 (and_6_out, A, not_5_out, not_6_out);
  and and_7 (and_7_out, A, B, Cin);
  or or_1 (Cout, and_1_out, and_2_out, and_3_out);
  or or_2 (Sum, and_4_out, and_5_out, and_6_out, and_7_out);
endmodule

module OverFlow (
  input  A,
  input  B,
  output R
);

  wire and_1_out, and_2_out, not_1_out, not_2_out;

  not not_1 (not_1_out, B);
  not not_2 (not_2_out, A);
  and and_1 (and_1_out, A, not_1_out);
  and and_2 (and_2_out, B, not_2_out);
  or or_1 (R, and_1_out, and_2_out);
endmodule

module SignCalculator (
  input  A,
  input  B,
  input  Overflow,
  output sgn
);

  Multiplexer #(.enable("false")) multiplexer_1 (.in0(A), .in1(B), .out(sgn), .sel(Overflow));
endmodule

module ALU_32bit (
  input  [2:0] ALU_Op,
  input  [31:0] b,
  input  [31:0] a,
  output [31:0] ALU_Result,
  output Zero
);

  wire Ainv, alu_1bit_1_cout, alu_1bit_2_cout, alu_1bit_3_cout, alu_1bit_4_cout, alu_1bit_5_cout,
       alu_1bit_6_cout, alu_1bit_7_cout, alu_1bit_8_cout, alu_1bit_9_cout, alu_1bit_10_cout,
       alu_1bit_11_cout, alu_1bit_12_cout, alu_1bit_13_cout, alu_1bit_14_cout, alu_1bit_15_cout,
       alu_1bit_16_cout, alu_1bit_17_cout, alu_1bit_18_cout, alu_1bit_19_cout, alu_1bit_20_cout,
       alu_1bit_21_cout, alu_1bit_22_cout, alu_1bit_23_cout, alu_1bit_24_cout, alu_1bit_25_cout,
       alu_1bit_26_cout, alu_1bit_27_cout, alu_1bit_28_cout, alu_1bit_29_cout, alu_1bit_30_cout,
       alu_1bit_31_cout, Binv, or_1_out, Sign;

  or or_1 (or_1_out, ALU_Result[0], ALU_Result[1], ALU_Result[2], ALU_Result[3], ALU_Result[4], ALU_Result[5], ALU_Result[6], ALU_Result[7], ALU_Result[8], ALU_Result[9], ALU_Result[10], ALU_Result[11], ALU_Result[12], ALU_Result[13], ALU_Result[14], ALU_Result[15], ALU_Result[16], ALU_Result[17], ALU_Result[18], ALU_Result[19], ALU_Result[20], ALU_Result[21], ALU_Result[22], ALU_Result[23], ALU_Result[24], ALU_Result[25], ALU_Result[26], ALU_Result[27], ALU_Result[28], ALU_Result[29], ALU_Result[30], ALU_Result[31]);
  not not_1 (Zero, or_1_out);
  Set_Ainv set_ainv_1 (.in_1(ALU_Op), .out_2(Ainv));
  Set_Binv set_binv_1 (.in_1(ALU_Op), .out_2(Binv));
  ALU_1bit alu_1bit_1 (
    .Cin(Binv), .A(a[0]), .B(b[0]), .ALU_Opt(ALU_Op), .Ainv(Ainv), .Binv(Binv), .SLT(Sign),
    .Result(ALU_Result[0]), .Cout(alu_1bit_1_cout));  // open: Sign
  ALU_1bit alu_1bit_2 (
    .Cin(alu_1bit_1_cout), .A(a[1]), .B(b[1]), .ALU_Opt(ALU_Op), .Ainv(Ainv), .Binv(Binv), .SLT(1'b0),
    .Result(ALU_Result[1]), .Cout(alu_1bit_2_cout));  // open: Sign
  ALU_1bit alu_1bit_3 (
    .Cin(alu_1bit_2_cout), .A(a[2]), .B(b[2]), .ALU_Opt(ALU_Op), .Ainv(Ainv), .Binv(Binv), .SLT(1'b0),
    .Result(ALU_Result[2]), .Cout(alu_1bit_3_cout));  // open: Sign
  ALU_1bit alu_1bit_4 (
    .Cin(alu_1bit_3_cout), .A(a[3]), .B(b[3]), .ALU_Opt(ALU_Op), .Ainv(Ainv), .Binv(Binv), .SLT(1'b0),
    .Result(ALU_Result[3]), .Cout(alu_1bit_4_cout));  // open: Sign
  ALU_1bit alu_1bit_5 (
    .Cin(alu_1bit_4_cout), .A(a[4]), .B(b[4]), .ALU_Opt(ALU_Op), .Ainv(Ainv), .Binv(Binv), .SLT(1'b0),
    .Result(ALU_Result[4]), .Cout(alu_1bit_5_cout));  // open: Sign
  ALU_1bit alu_1bit_6 (
    .Cin(alu_1bit_5_cout), .A(a[5]), .B(b[5]), .ALU_Opt(ALU_Op), .Ainv(Ainv), .Binv(Binv), .SLT(1'b0),
    .Result(ALU_Result[5]), .Cout(alu_1bit_6_cout));  // open: Sign
  ALU_1bit alu_1bit_7 (
    .Cin(alu_1bit_6_cout), .A(a[6]), .B(b[6]), .ALU_Opt(ALU_Op), .Ainv(Ainv), .Binv(Binv), .SLT(1'b0),
    .Result(ALU_Result[6]), .Cout(alu_1bit_7_cout));  // open: Sign
  ALU_1bit alu_1bit_8 (
    .Cin(alu_1bit_7_cout), .A(a[7]), .B(b[7]), .ALU_Opt(ALU_Op), .Ainv(Ainv), .Binv(Binv), .SLT(1'b0),
    .Result(ALU_Result[7]), .Cout(alu_1bit_8_cout));  // open: Sign
  ALU_1bit alu_1bit_9 (
    .Cin(alu_1bit_8_cout), .A(a[8]), .B(b[8]), .ALU_Opt(ALU_Op), .Ainv(Ainv), .Binv(Binv), .SLT(1'b0),
    .Result(ALU_Result[8]), .Cout(alu_1bit_9_cout));  // open: Sign
  ALU_1bit alu_1bit_10 (
    .Cin(alu_1bit_9_cout), .A(a[9]), .B(b[9]), .ALU_Opt(ALU_Op), .Ainv(Ainv), .Binv(Binv), .SLT(1'b0),
    .Result(ALU_Result[9]), .Cout(alu_1bit_10_cout));  // open: Sign
  ALU_1bit alu_1bit_11 (
    .Cin(alu_1bit_10_cout), .A(a[10]), .B(b[10]), .ALU_Opt(ALU_Op), .Ainv(Ainv), .Binv(Binv), .SLT(1'b0),
    .Result(ALU_Result[10]), .Cout(alu_1bit_11_cout));  // open: Sign
  ALU_1bit alu_1bit_12 (
    .Cin(alu_1bit_11_cout), .A(a[11]), .B(b[11]), .ALU_Opt(ALU_Op), .Ainv(Ainv), .Binv(Binv), .SLT(1'b0),
    .Result(ALU_Result[11]), .Cout(alu_1bit_12_cout));  // open: Sign
  ALU_1bit alu_1bit_13 (
    .Cin(alu_1bit_12_cout), .A(a[12]), .B(b[12]), .ALU_Opt(ALU_Op), .Ainv(Ainv), .Binv(Binv), .SLT(1'b0),
    .Result(ALU_Result[12]), .Cout(alu_1bit_13_cout));  // open: Sign
  ALU_1bit alu_1bit_14 (
    .Cin(alu_1bit_13_cout), .A(a[13]), .B(b[13]), .ALU_Opt(ALU_Op), .Ainv(Ainv), .Binv(Binv), .SLT(1'b0),
    .Result(ALU_Result[13]), .Cout(alu_1bit_14_cout));  // open: Sign
  ALU_1bit alu_1bit_15 (
    .Cin(alu_1bit_14_cout), .A(a[14]), .B(b[14]), .ALU_Opt(ALU_Op), .Ainv(Ainv), .Binv(Binv), .SLT(1'b0),
    .Result(ALU_Result[14]), .Cout(alu_1bit_15_cout));  // open: Sign
  ALU_1bit alu_1bit_16 (
    .Cin(alu_1bit_15_cout), .A(a[15]), .B(b[15]), .ALU_Opt(ALU_Op), .Ainv(Ainv), .Binv(Binv), .SLT(1'b0),
    .Result(ALU_Result[15]), .Cout(alu_1bit_16_cout));  // open: Sign
  ALU_1bit alu_1bit_17 (
    .Cin(alu_1bit_16_cout), .A(a[16]), .B(b[16]), .ALU_Opt(ALU_Op), .Ainv(Ainv), .Binv(Binv), .SLT(1'b0),
    .Result(ALU_Result[16]), .Cout(alu_1bit_17_cout));  // open: Sign
  ALU_1bit alu_1bit_18 (
    .Cin(alu_1bit_17_cout), .A(a[17]), .B(b[17]), .ALU_Opt(ALU_Op), .Ainv(Ainv), .Binv(Binv), .SLT(1'b0),
    .Result(ALU_Result[17]), .Cout(alu_1bit_18_cout));  // open: Sign
  ALU_1bit alu_1bit_19 (
    .Cin(alu_1bit_18_cout), .A(a[18]), .B(b[18]), .ALU_Opt(ALU_Op), .Ainv(Ainv), .Binv(Binv), .SLT(1'b0),
    .Result(ALU_Result[18]), .Cout(alu_1bit_19_cout));  // open: Sign
  ALU_1bit alu_1bit_20 (
    .Cin(alu_1bit_19_cout), .A(a[19]), .B(b[19]), .ALU_Opt(ALU_Op), .Ainv(Ainv), .Binv(Binv), .SLT(1'b0),
    .Result(ALU_Result[19]), .Cout(alu_1bit_20_cout));  // open: Sign
  ALU_1bit alu_1bit_21 (
    .Cin(alu_1bit_20_cout), .A(a[20]), .B(b[20]), .ALU_Opt(ALU_Op), .Ainv(Ainv), .Binv(Binv), .SLT(1'b0),
    .Result(ALU_Result[20]), .Cout(alu_1bit_21_cout));  // open: Sign
  ALU_1bit alu_1bit_22 (
    .Cin(alu_1bit_21_cout), .A(a[21]), .B(b[21]), .ALU_Opt(ALU_Op), .Ainv(Ainv), .Binv(Binv), .SLT(1'b0),
    .Result(ALU_Result[21]), .Cout(alu_1bit_22_cout));  // open: Sign
  ALU_1bit alu_1bit_23 (
    .Cin(alu_1bit_22_cout), .A(a[22]), .B(b[22]), .ALU_Opt(ALU_Op), .Ainv(Ainv), .Binv(Binv), .SLT(1'b0),
    .Result(ALU_Result[22]), .Cout(alu_1bit_23_cout));  // open: Sign
  ALU_1bit alu_1bit_24 (
    .Cin(alu_1bit_23_cout), .A(a[23]), .B(b[23]), .ALU_Opt(ALU_Op), .Ainv(Ainv), .Binv(Binv), .SLT(1'b0),
    .Result(ALU_Result[23]), .Cout(alu_1bit_24_cout));  // open: Sign
  ALU_1bit alu_1bit_25 (
    .Cin(alu_1bit_24_cout), .A(a[24]), .B(b[24]), .ALU_Opt(ALU_Op), .Ainv(Ainv), .Binv(Binv), .SLT(1'b0),
    .Result(ALU_Result[24]), .Cout(alu_1bit_25_cout));  // open: Sign
  ALU_1bit alu_1bit_26 (
    .Cin(alu_1bit_25_cout), .A(a[25]), .B(b[25]), .ALU_Opt(ALU_Op), .Ainv(Ainv), .Binv(Binv), .SLT(1'b0),
    .Result(ALU_Result[25]), .Cout(alu_1bit_26_cout));  // open: Sign
  ALU_1bit alu_1bit_27 (
    .Cin(alu_1bit_26_cout), .A(a[26]), .B(b[26]), .ALU_Opt(ALU_Op), .Ainv(Ainv), .Binv(Binv), .SLT(1'b0),
    .Result(ALU_Result[26]), .Cout(alu_1bit_27_cout));  // open: Sign
  ALU_1bit alu_1bit_28 (
    .Cin(alu_1bit_27_cout), .A(a[27]), .B(b[27]), .ALU_Opt(ALU_Op), .Ainv(Ainv), .Binv(Binv), .SLT(1'b0),
    .Result(ALU_Result[27]), .Cout(alu_1bit_28_cout));  // open: Sign
  ALU_1bit alu_1bit_29 (
    .Cin(alu_1bit_28_cout), .A(a[28]), .B(b[28]), .ALU_Opt(ALU_Op), .Ainv(Ainv), .Binv(Binv), .SLT(1'b0),
    .Result(ALU_Result[28]), .Cout(alu_1bit_29_cout));  // open: Sign
  ALU_1bit alu_1bit_30 (
    .Cin(alu_1bit_29_cout), .A(a[29]), .B(b[29]), .ALU_Opt(ALU_Op), .Ainv(Ainv), .Binv(Binv), .SLT(1'b0),
    .Result(ALU_Result[29]), .Cout(alu_1bit_30_cout));  // open: Sign
  ALU_1bit alu_1bit_31 (
    .Cin(alu_1bit_30_cout), .A(a[30]), .B(b[30]), .ALU_Opt(ALU_Op), .Ainv(Ainv), .Binv(Binv), .SLT(1'b0),
    .Result(ALU_Result[30]), .Cout(alu_1bit_31_cout));  // open: Sign
  ALU_1bit alu_1bit_32 (
    .Cin(alu_1bit_31_cout), .A(a[31]), .B(b[31]), .ALU_Opt(ALU_Op), .Ainv(Ainv), .Binv(Binv), .SLT(1'b0),
    .Result(ALU_Result[31]), .Sign(Sign));  // open: Cout

  // Other names for the same wires on the sheet: R0 = ALU_Result[0]; R1 = ALU_Result[1]; R2 = ALU_Result[2];
  //   R3 = ALU_Result[3]; R4 = ALU_Result[4]; R5 = ALU_Result[5]; R6 = ALU_Result[6]; R7 = ALU_Result[7];
  //   R8 = ALU_Result[8]; R9 = ALU_Result[9]; R10 = ALU_Result[10]; R11 = ALU_Result[11]; R12 = ALU_Result[12];
  //   R13 = ALU_Result[13]; R14 = ALU_Result[14]; R15 = ALU_Result[15]; R16 = ALU_Result[16]; R17 = ALU_Result[17];
  //   R18 = ALU_Result[18]; R19 = ALU_Result[19]; R20 = ALU_Result[20]; R21 = ALU_Result[21]; R22 = ALU_Result[22];
  //   R23 = ALU_Result[23]; R24 = ALU_Result[24]; R25 = ALU_Result[25]; R26 = ALU_Result[26]; R27 = ALU_Result[27];
  //   R28 = ALU_Result[28]; R29 = ALU_Result[29]; R30 = ALU_Result[30]; R31 = ALU_Result[31]
endmodule

module Decoder_ALU (
  input  in_1,
  input  in_2,
  input  in_3,
  output [1:0] out_4
);

  wire and_1_out, and_2_out, BNEG;

  and and_1 (and_1_out, in_1, in_3);
  not not_1 (BNEG, in_2);
  and and_2 (and_2_out, in_1, BNEG);
  or or_1 (out_4[0], and_2_out, and_1_out);

  assign out_4[1] = in_2;

  // Other names for the same wires on the sheet: A = in_1; C = in_3; B = in_2
endmodule

module ALU_4bits (
  input  [3:0] a,
  input  [3:0] b,
  input  [2:0] Alu_Op,
  output [3:0] R
);

  wire Ainv, alu_1bit_1_cout, alu_1bit_2_cout, alu_1bit_3_cout, Binv, Sign;

  Set_Ainv set_ainv_1 (.in_1(Alu_Op), .out_2(Ainv));
  Set_Binv set_binv_1 (.in_1(Alu_Op), .out_2(Binv));
  ALU_1bit alu_1bit_1 (
    .Cin(Binv), .A(a[0]), .B(b[0]), .ALU_Opt(Alu_Op), .Ainv(Ainv), .Binv(Binv), .SLT(Sign), .Result(R[0]),
    .Cout(alu_1bit_1_cout));  // open: Sign
  ALU_1bit alu_1bit_2 (
    .Cin(alu_1bit_1_cout), .A(a[1]), .B(b[1]), .ALU_Opt(Alu_Op), .Ainv(Ainv), .Binv(Binv), .SLT(1'b0),
    .Result(R[1]), .Cout(alu_1bit_2_cout));  // open: Sign
  ALU_1bit alu_1bit_3 (
    .Cin(alu_1bit_2_cout), .A(a[2]), .B(b[2]), .ALU_Opt(Alu_Op), .Ainv(Ainv), .Binv(Binv), .SLT(1'b0),
    .Result(R[2]), .Cout(alu_1bit_3_cout));  // open: Sign
  ALU_1bit alu_1bit_4 (
    .Cin(alu_1bit_3_cout), .A(a[3]), .B(b[3]), .ALU_Opt(Alu_Op), .Ainv(Ainv), .Binv(Binv), .SLT(1'b0),
    .Result(R[3]), .Sign(Sign));  // open: Cout
endmodule

module Set_Ainv (
  input  [2:0] in_1,
  output out_2
);

  wire not_1_out;

  not not_1 (not_1_out, in_1[1]);
  and and_1 (out_2, in_1[0], not_1_out);
endmodule

module Set_Binv (
  input  [2:0] in_1,
  output out_2
);

  wire and_1_out, and_2_out, not_1_out;

  not not_1 (not_1_out, in_1[1]);
  and and_1 (and_1_out, in_1[2], in_1[1]);
  and and_2 (and_2_out, not_1_out, in_1[0]);
  or or_1 (out_2, and_1_out, and_2_out);
endmodule

module ALU_Control (
  input  [1:0] ALUOp,
  input  [5:0] func,
  output [2:0] ALU_Oper
);

  wire and_1_out, and_2_out, and_3_out, and_4_out, and_5_out, and_6_out, and_7_out, and_8_out, and_9_out,
       and_10_out, and_11_out, and_12_out, and_13_out, and_14_out, and_15_out, Aneg, Bneg, Cneg, Dneg, Eneg,
       Fneg, Gneg, Hneg, or_1_out, or_2_out, or_5_out;

  not not_1 (Aneg, ALUOp[1]);
  not not_2 (Bneg, ALUOp[0]);
  not not_3 (Gneg, func[1]);
  not not_4 (Hneg, func[0]);
  not not_5 (Cneg, func[5]);
  not not_6 (Dneg, func[4]);
  not not_7 (Eneg, func[3]);
  not not_8 (Fneg, func[2]);
  and and_1 (and_1_out, Eneg, func[2], Gneg, func[0]);
  and and_2 (and_2_out, Fneg, func[1], Hneg);
  and and_3 (and_3_out, Eneg, func[2], func[1], func[0]);
  and and_4 (and_4_out, Eneg, Fneg, Gneg, Hneg);
  and and_5 (and_5_out, func[3], Fneg, func[1], Hneg);
  and and_6 (and_6_out, ALUOp[1], Bneg, func[5], Dneg);
  or or_1 (or_1_out, and_1_out, and_2_out);
  and and_7 (and_7_out, ALUOp[1], Bneg, func[5], Dneg);
  or or_2 (or_2_out, and_4_out, and_3_out, and_5_out);
  and and_8 (and_8_out, Aneg, ALUOp[0]);
  and and_9 (and_9_out, and_6_out, or_1_out);
  and and_10 (and_10_out, Aneg, Bneg);
  and and_11 (and_11_out, and_7_out, or_2_out);
  or or_3 (ALU_Oper[2], and_8_out, and_9_out);
  or or_4 (ALU_Oper[0], and_10_out, and_11_out);
  and and_12 (and_12_out, Eneg, Fneg, Hneg);
  and and_13 (and_13_out, Fneg, func[1], Hneg);
  and and_14 (and_14_out, ALUOp[1], Bneg, func[5], Dneg);
  or or_5 (or_5_out, and_12_out, and_13_out);
  and and_15 (and_15_out, and_14_out, or_5_out);
  or or_6 (ALU_Oper[1], Aneg, and_15_out);

  // Other names for the same wires on the sheet: Z = ALU_Oper[0]; Y = ALU_Oper[1]; X = ALU_Oper[2]; B = ALUOp[0];
  //   A = ALUOp[1]; H = func[0]; G = func[1]; F = func[2]; E = func[3]; D = func[4]; C = func[5]
endmodule

module MAIN_CONTROL (
  input  [5:0] OpCode,
  output Regdst,
  output ALUSrc,
  output MemtoReg,
  output RegWrite,
  output MemRead,
  output MemWrite,
  output Branch,
  output [1:0] ALUOp,
  output jump,
  output link
);

  wire Aneg, Bneg, Cneg, Dneg, Eneg, Fneg;

  not not_1 (Aneg, OpCode[5]);
  not not_2 (Eneg, OpCode[1]);
  not not_3 (Fneg, OpCode[0]);
  not not_4 (Bneg, OpCode[4]);
  not not_5 (Cneg, OpCode[3]);
  not not_6 (Dneg, OpCode[2]);
  and and_1 (jump, Aneg, OpCode[1]);
  and and_2 (link, Aneg, OpCode[0]);
  and and_3 (RegWrite, Cneg, Dneg);
  and and_4 (Regdst, Aneg, Bneg, Cneg, Dneg, Eneg, Fneg);
  and and_5 (ALUSrc, OpCode[5], Bneg, Dneg, OpCode[1], OpCode[0]);
  and and_6 (MemtoReg, OpCode[5], Bneg, Cneg, Dneg, OpCode[1], OpCode[0]);
  and and_7 (MemRead, OpCode[5], Bneg, Cneg, Dneg, OpCode[1], OpCode[0]);
  and and_8 (MemWrite, OpCode[5], Bneg, OpCode[3], Dneg, OpCode[1], OpCode[0]);
  and and_9 (Branch, Aneg, Bneg, Cneg, OpCode[2], Eneg, Fneg);
  and and_10 (ALUOp[1], Aneg, Bneg, Cneg, Dneg, Eneg, Fneg);
  and and_11 (ALUOp[0], Aneg, Bneg, Cneg, OpCode[2], Eneg, Fneg);

  // Other names for the same wires on the sheet: F = OpCode[0]; E = OpCode[1]; D = OpCode[2]; C = OpCode[3];
  //   B = OpCode[4]; A = OpCode[5]
endmodule

module Reg_File (
  input  CLK,
  input  Reset,
  input  [31:0] Write_Data,
  input  [4:0] Read_Reg_1,
  input  [4:0] Read_Reg_2,
  input  Reg_Write,
  input  [4:0] Write_Reg,
  output [31:0] RD1,
  output [31:0] RD2
);

  wire decoder_1_out0, decoder_1_out1, decoder_1_out2, decoder_1_out3, decoder_1_out4, decoder_1_out5,
       decoder_1_out6, decoder_1_out7, decoder_1_out8, decoder_1_out9, decoder_1_out10, decoder_1_out11,
       decoder_1_out12, decoder_1_out13, decoder_1_out14, decoder_1_out15, decoder_1_out16, decoder_1_out17,
       decoder_1_out18, decoder_1_out19, decoder_1_out20, decoder_1_out21, decoder_1_out22, decoder_1_out23,
       decoder_1_out24, decoder_1_out25, decoder_1_out26, decoder_1_out27, decoder_1_out28, decoder_1_out29,
       decoder_1_out30, decoder_1_out31;
  wire [31:0] R0, R1, R2, R3, R4, R5, R6, R7, R8, R9, R10, R11, R12, R13, R14, R15, R16, R17, R18, R19, R20,
       R21, R22, R23, R24, R25, R26, R27, R28, R29, R30, R31;

  Decoder #(.select(5)) decoder_1 (
    .out0(decoder_1_out0), .out1(decoder_1_out1), .out2(decoder_1_out2), .out3(decoder_1_out3),
    .out4(decoder_1_out4), .out5(decoder_1_out5), .out6(decoder_1_out6), .out7(decoder_1_out7),
    .out8(decoder_1_out8), .out9(decoder_1_out9), .out10(decoder_1_out10), .out11(decoder_1_out11),
    .out12(decoder_1_out12), .out13(decoder_1_out13), .out14(decoder_1_out14), .out15(decoder_1_out15),
    .out16(decoder_1_out16), .out17(decoder_1_out17), .out18(decoder_1_out18), .out19(decoder_1_out19),
    .out20(decoder_1_out20), .out21(decoder_1_out21), .out22(decoder_1_out22), .out23(decoder_1_out23),
    .out24(decoder_1_out24), .out25(decoder_1_out25), .out26(decoder_1_out26), .out27(decoder_1_out27),
    .out28(decoder_1_out28), .out29(decoder_1_out29), .out30(decoder_1_out30), .out31(decoder_1_out31),
    .sel(Write_Reg), .en(Reg_Write));
  Register #(.width(32)) register_1 (.D(Write_Data), .en(decoder_1_out0), .clk(CLK), .Q(R0), .clr(Reset));
  Register #(.width(32)) register_2 (.D(Write_Data), .en(decoder_1_out1), .clk(CLK), .Q(R1), .clr(Reset));
  Register #(.width(32)) register_3 (.D(Write_Data), .en(decoder_1_out2), .clk(CLK), .Q(R2), .clr(Reset));
  Register #(.width(32)) register_4 (.D(Write_Data), .en(decoder_1_out3), .clk(CLK), .Q(R3), .clr(Reset));
  Register #(.width(32)) register_5 (.D(Write_Data), .en(decoder_1_out4), .clk(CLK), .Q(R4), .clr(Reset));
  Register #(.width(32)) register_6 (.D(Write_Data), .en(decoder_1_out5), .clk(CLK), .Q(R5), .clr(Reset));
  Register #(.width(32)) register_7 (.D(Write_Data), .en(decoder_1_out6), .clk(CLK), .Q(R6), .clr(Reset));
  Register #(.width(32)) register_8 (.D(Write_Data), .en(decoder_1_out7), .clk(CLK), .Q(R7), .clr(Reset));
  Register #(.width(32)) register_9 (.D(Write_Data), .en(decoder_1_out8), .clk(CLK), .Q(R8), .clr(Reset));
  Register #(.width(32)) register_10 (.D(Write_Data), .en(decoder_1_out9), .clk(CLK), .Q(R9), .clr(Reset));
  Register #(.width(32)) register_11 (.D(Write_Data), .en(decoder_1_out10), .clk(CLK), .Q(R10), .clr(Reset));
  Register #(.width(32)) register_12 (.D(Write_Data), .en(decoder_1_out11), .clk(CLK), .Q(R11), .clr(Reset));
  Register #(.width(32)) register_13 (.D(Write_Data), .en(decoder_1_out12), .clk(CLK), .Q(R12), .clr(Reset));
  Register #(.width(32)) register_14 (.D(Write_Data), .en(decoder_1_out13), .clk(CLK), .Q(R13), .clr(Reset));
  Register #(.width(32)) register_15 (.D(Write_Data), .en(decoder_1_out14), .clk(CLK), .Q(R14), .clr(Reset));
  Register #(.width(32)) register_16 (.D(Write_Data), .en(decoder_1_out15), .clk(CLK), .Q(R15), .clr(Reset));
  Register #(.width(32)) register_17 (.D(Write_Data), .en(decoder_1_out16), .clk(CLK), .Q(R16), .clr(Reset));
  Register #(.width(32)) register_18 (.D(Write_Data), .en(decoder_1_out17), .clk(CLK), .Q(R17), .clr(Reset));
  Register #(.width(32)) register_19 (.D(Write_Data), .en(decoder_1_out18), .clk(CLK), .Q(R18), .clr(Reset));
  Register #(.width(32)) register_20 (.D(Write_Data), .en(decoder_1_out19), .clk(CLK), .Q(R19), .clr(Reset));
  Register #(.width(32)) register_21 (.D(Write_Data), .en(decoder_1_out20), .clk(CLK), .Q(R20), .clr(Reset));
  Register #(.width(32)) register_22 (.D(Write_Data), .en(decoder_1_out21), .clk(CLK), .Q(R21), .clr(Reset));
  Register #(.width(32)) register_23 (.D(Write_Data), .en(decoder_1_out22), .clk(CLK), .Q(R22), .clr(Reset));
  Register #(.width(32)) register_24 (.D(Write_Data), .en(decoder_1_out23), .clk(CLK), .Q(R23), .clr(Reset));
  Register #(.width(32)) register_25 (.D(Write_Data), .en(decoder_1_out24), .clk(CLK), .Q(R24), .clr(Reset));
  Register #(.width(32)) register_26 (.D(Write_Data), .en(decoder_1_out25), .clk(CLK), .Q(R25), .clr(Reset));
  Register #(.width(32)) register_27 (.D(Write_Data), .en(decoder_1_out26), .clk(CLK), .Q(R26), .clr(Reset));
  Register #(.width(32)) register_28 (.D(Write_Data), .en(decoder_1_out27), .clk(CLK), .Q(R27), .clr(Reset));
  Register #(.width(32)) register_29 (.D(Write_Data), .en(decoder_1_out28), .clk(CLK), .Q(R28), .clr(Reset));
  Register #(.width(32)) register_30 (.D(Write_Data), .en(decoder_1_out29), .clk(CLK), .Q(R29), .clr(Reset));
  Register #(.width(32)) register_31 (.D(Write_Data), .en(decoder_1_out30), .clk(CLK), .Q(R30), .clr(Reset));
  Register #(.width(32)) register_32 (.D(Write_Data), .en(decoder_1_out31), .clk(CLK), .Q(R31), .clr(Reset));
  Multiplexer #(.select(5), .width(32), .enable("false")) multiplexer_1 (
    .in0(R0), .in1(R1), .in2(R2), .in3(R3), .in4(R4), .in5(R5), .in6(R6), .in7(R7), .in8(R8), .in9(R9),
    .in10(R10), .in11(R11), .in12(R12), .in13(R13), .in14(R14), .in15(R15), .in16(R16), .in17(R17),
    .in18(R18), .in19(R19), .in20(R20), .in21(R21), .in22(R22), .in23(R23), .in24(R24), .in25(R25),
    .in26(R26), .in27(R27), .in28(R28), .in29(R29), .in30(R30), .in31(R31), .out(RD1), .sel(Read_Reg_1));
  Multiplexer #(.select(5), .width(32), .enable("false")) multiplexer_2 (
    .in0(R0), .in1(R1), .in2(R2), .in3(R3), .in4(R4), .in5(R5), .in6(R6), .in7(R7), .in8(R8), .in9(R9),
    .in10(R10), .in11(R11), .in12(R12), .in13(R13), .in14(R14), .in15(R15), .in16(R16), .in17(R17),
    .in18(R18), .in19(R19), .in20(R20), .in21(R21), .in22(R22), .in23(R23), .in24(R24), .in25(R25),
    .in26(R26), .in27(R27), .in28(R28), .in29(R29), .in30(R30), .in31(R31), .out(RD2), .sel(Read_Reg_2));

  // Other names for the same wires on the sheet: RR1[4:0] = Read_Reg_1; RR2[4:0] = Read_Reg_2
endmodule

module Instruction_memory (
  input  [31:0] Addr,
  output [31:0] Instr
);

  ROM #(.addrWidth(24), .dataWidth(32)) rom_1 (.addr(Addr[25:2]), .data(Instr));
endmodule

module PC (
  input  [31:0] Addr,
  input  CLK,
  input  RESET,
  output [31:0] Out_Addr
);

  Register #(.width(32)) register_1 (.D(Addr), .en(1'b1), .clk(CLK), .Q(Out_Addr), .clr(RESET));

  // Other names for the same wires on the sheet: add[31:0] = Addr
endmodule

module InstDecoder (
  input  [31:0] in_1,
  output [5:0] OpCode,
  output [4:0] rs,
  output [4:0] rt,
  output [4:0] rd,
  output [5:0] funct,
  output [15:0] address,
  output [25:0] add_26
);


  assign add_26 = in_1[25:0];
  assign address = in_1[15:0];
  assign funct = in_1[5:0];
  assign OpCode = in_1[31:26];
  assign rd = in_1[15:11];
  assign rs = in_1[25:21];
  assign rt = in_1[20:16];
endmodule

module Data_memory (
  input  [31:0] Address,
  input  [31:0] Write_data,
  input  MemRead,
  input  MemWrite,
  input  Clk,
  output [31:0] Read_data
);

  RAM #(.addrWidth(24), .dataWidth(32)) ram_1 (
    .addr(Address[25:2]), .we(MemWrite), .oe(MemRead), .clk(Clk), .data(Read_data));
endmodule

module Decoder_jr (
  input  [1:0] in_1,
  input  [5:0] in_2,
  output jr
);

  wire and_1_out, and_2_out;

  and and_1 (and_1_out, ~in_1[0], in_1[1]);  // AND_Gate
  and and_2 (and_2_out, ~in_2[0], ~in_2[1], in_2[2], ~in_2[3], ~in_2[4], ~in_2[5]);  // AND_Gate
  and and_3 (jr, and_1_out, and_2_out);
endmodule
