// Logisim project lab4.circ as structural Verilog: 12 circuits, main circuit main
module main (
  input  A,
  input  B,
  input  C,
  output [1:0] out_4
);

  wire and_1_out, and_2_out, BNEG;

  and and_1 (and_1_out, A, C);
  not not_1 (BNEG, B);
  and and_2 (and_2_out, A, BNEG);
  or or_1 (out_4[0], and_2_out, and_1_out);

  assign out_4[1] = B;
endmodule

module ALU_1bit (
  input  Cin,
  input  A,
  input  B,
  input  [2:0] ALU_Opt,
  input  Ainv,
  input  Binv,
  input  SLT,
  output Result,
  output Cout,
  output Sign
);

  wire A_neg, Aop, B_neg, Bop, overflow_1_r, r_and, r_or, r_sum;
  wire [1:0] decoder_alu_1_out_4;

  not not_1 (A_neg, A);
  not not_2 (B_neg, B);
  Multiplexer #(.enable("false")) multiplexer_1 (.in0(A), .in1(A_neg), .out(Aop), .sel(Ainv));
  Multiplexer #(.enable("false")) multiplexer_2 (.in0(B), .in1(B_neg), .out(Bop), .sel(Binv));
  OverFlow overflow_1 (.A(Cin), .B(Cout), .R(overflow_1_r));
  or or_1 (r_or, Aop, Bop);
  and and_1 (r_and, Aop, Bop);
  FA_1bit fa_1bit_1 (.A(Aop), .B(Bop), .Cin(Cin), .Sum(r_sum), .Cout(Cout));
  SignCalculator signcalculator_1 (.A(r_sum), .B(Cout), .Overflow(overflow_1_r), .sgn(Sign));
  Multiplexer #(.select(2), .enable("false")) multiplexer_3 (
    .in0(r_and), .in1(r_or), .in2(r_sum), .in3(SLT), .out(Result), .sel(decoder_alu_1_out_4));
  Decoder_ALU decoder_alu_1 (.in_1(ALU_Opt[2]), .in_2(ALU_Opt[1]), .in_3(ALU_Opt[0]), .out_4(decoder_alu_1_out_4));

  // Other names for the same wires on the sheet: r_slt = SLT
endmodule

module FA_1bit (
  input  A,
  input  B,
  input  Cin,
  output Sum,
  output Cout
);

  wire and_1_out, and_2_out, and_3_out, and_4_out, and_5_out, and_6_out, and_7_out, not_1_out, not_2_out,
       not_3_out, not_4_out, not_5_out, not_6_out;

  not not_1 (not_1_out, A);
  not not_2 (not_2_out, B);
  not not_3 (not_3_out, A);
  not not_4 (not_4_out, Cin);
  not not_5 (not_5_out, B);
  not not_6 (not_6_out, Cin);
  and and_1 (and_1_out, B, Cin);
  and and_2 (and_2_out, A, Cin);
  and and_3 (and_3_out, A, B);
  and and_4 (and_4_out, not_1_out, not_2_out, Cin);
  and and_5 (and_5_out, not_3_out, B, not_4_out);
  and and_6 (and_6_out, A, not_5_out, not_6_out);
  and and_7 (and_7_out, A, B, Cin);
  or or_1 (Cout, and_1_out, and_2_out, and_3_out);
  or or_2 (Sum, and_4_out, and_5_out, and_6_out, and_7_out);
endmodule

module OverFlow (
  input  A,
  input  B,
  output R
);

  wire and_1_out, and_2_out, not_1_out, not_2_out;

  not not_1 (not_1_out, B);
  not not_2 (not_2_out, A);
  and and_1 (and_1_out, A, not_1_out);
  and and_2 (and_2_out, B, not_2_out);
  or or_1 (R, and_1_out, and_2_out);
endmodule

module SignCalculator (
  input  A,
  input  B,
  input  Overflow,
  output sgn
);

  Multiplexer #(.enable("false")) multiplexer_1 (.in0(A), .in1(B), .out(sgn), .sel(Overflow));
endmodule

module ALU_32bit (
  input  [3:0] ALU_Operation,
  input  [31:0] a,
  input  [31:0] b,
  output out_4,
  output [31:0] R
);


  assign out_4 = 1'b0;

  // Other names for the same wires on the sheet: b0 = a[0]; b1 = a[1]; b2 = a[2]; b3 = a[3]; b4 = a[4]; b5 = a[5];
  //   b6 = a[6]; b7 = a[7]; b8 = a[8]; b9 = a[9]; b10 = a[10]; b11 = a[11]; b12 = a[12]; b13 = a[13]; b14 = a[14];
  //   b15 = a[15]; b16 = a[16]; b17 = a[17]; b18 = a[18]; b19 = a[19]; b20 = a[20]; b21 = a[21]; b22 = a[22];
  //   b23 = a[23]; b24 = a[24]; b25 = a[25]; b26 = a[26]; b27 = a[27]; b28 = a[28]; b29 = a[29]; b30 = a[30];
  //   b31 = a[31]; ALU_Opt0 = ALU_Operation[0]; ALU_Opt1 = ALU_Operation[1]; binv = ALU_Operation[2];
  //   ainv = ALU_Operation[3]; a0 = b[0]; a1 = b[1]; a2 = b[2]; a3 = b[3]; a4 = b[4]; a5 = b[5]; a6 = b[6]; a7 = b[7];
  //   a8 = b[8]; a9 = b[9]; a10 = b[10]; a11 = b[11]; a12 = b[12]; a13 = b[13]; a14 = b[14]; a15 = b[15]; a16 = b[16];
  //   a17 = b[17]; a18 = b[18]; a19 = b[19]; a20 = b[20]; a21 = b[21]; a22 = b[22]; a23 = b[23]; a24 = b[24];
  //   a25 = b[25]; a26 = b[26]; a27 = b[27]; a28 = b[28]; a29 = b[29]; a30 = b[30]; a31 = b[31]
endmodule

module Decoder_ALU (
  input  in_1,
  input  in_2,
  input  in_3,
  output [1:0] out_4
);

  wire and_1_out, and_2_out, BNEG;

  and and_1 (and_1_out, in_1, in_3);
  not not_1 (BNEG, in_2);
  and and_2 (and_2_out, in_1, BNEG);
  or or_1 (out_4[0], and_2_out, and_1_out);

  assign out_4[1] = in_2;

  // Other names for the same wires on the sheet: A = in_1; C = in_3; B = in_2
endmodule

module ALU_4bits (
  input  [3:0] a,
  input  [3:0] b,
  input  [2:0] Alu_Op,
  output [3:0] R
);

  wire Ainv, alu_1bit_1_cout, alu_1bit_2_cout, alu_1bit_3_cout, Binv, Sign;

  Set_Ainv set_ainv_1 (.in_1(Alu_Op), .out_2(Ainv));
  Set_Binv set_binv_1 (.in_1(Alu_Op), .out_2(Binv));
  ALU_1bit alu_1bit_1 (
    .Cin(Binv), .A(a[0]), .B(b[0]), .ALU_Opt(Alu_Op), .Ainv(Ainv), .Binv(Binv), .SLT(Sign), .Result(R[0]),
    .Cout(alu_1bit_1_cout));  // open: Sign
  ALU_1bit alu_1bit_2 (
    .Cin(alu_1bit_1_cout), .A(a[1]), .B(b[1]), .ALU_Opt(Alu_Op), .Ainv(Ainv), .Binv(Binv), .SLT(1'b0),
    .Result(R[1]), .Cout(alu_1bit_2_cout));  // open: Sign
  ALU_1bit alu_1bit_3 (
    .Cin(alu_1bit_2_cout), .A(a[2]), .B(b[2]), .ALU_Opt(Alu_Op), .Ainv(Ainv), .Binv(Binv), .SLT(1'b0),
    .Result(R[2]), .Cout(alu_1bit_3_cout));  // open: Sign
  ALU_1bit alu_1bit_4 (
    .Cin(alu_1bit_3_cout), .A(a[3]), .B(b[3]), .ALU_Opt(Alu_Op), .Ainv(Ainv), .Binv(Binv), .SLT(1'b0),
    .Result(R[3]), .Sign(Sign));  // open: Cout
endmodule

module Set_Ainv (
  input  [2:0] in_1,
  output out_2
);

  wire not_1_out;

  not not_1 (not_1_out, in_1[1]);
  and and_1 (out_2, in_1[0], not_1_out);
endmodule

module Set_Binv (
  input  [2:0] in_1,
  output out_2
);

  wire and_1_out, and_2_out, not_1_out;

  not not_1 (not_1_out, in_1[1]);
  and and_1 (and_1_out, in_1[2], in_1[1]);
  and and_2 (and_2_out, not_1_out, in_1[0]);
  or or_1 (out_2, and_1_out, and_2_out);
endmodule

module ALU_Control (
  input  Op1,
  input  Op0,
  input  Func5,
  input  Func4,
  input  Func3,
  input  Func2,
  input  Func1,
  input  Func0,
  output [2:0] out_9
);

  wire and_1_out, and_2_out, and_3_out, and_4_out, and_5_out, and_6_out, and_7_out, and_8_out, and_9_out,
       and_10_out, and_11_out, and_12_out, and_13_out, and_14_out, and_15_out, Aneg, Bneg, Cneg, Dneg, Eneg,
       Fneg, Gneg, Hneg, or_1_out, or_2_out, or_5_out;

  not not_1 (Aneg, Op1);
  not not_2 (Bneg, Op0);
  not not_3 (Cneg, Func5);
  not not_4 (Dneg, Func4);
  not not_5 (Eneg, Func3);
  not not_6 (Fneg, Func2);
  not not_7 (Gneg, Func1);
  not not_8 (Hneg, Func0);
  and and_1 (and_1_out, Eneg, Func2, Gneg, Func0);
  and and_2 (and_2_out, Fneg, Func1, Hneg);
  and and_3 (and_3_out, Eneg, Func2, Func1, Func0);
  and and_4 (and_4_out, Eneg, Fneg, Gneg, Hneg);
  and and_5 (and_5_out, Func3, Fneg, Func1, Hneg);
  and and_6 (and_6_out, Op1, Bneg, Func5, Dneg);
  or or_1 (or_1_out, and_1_out, and_2_out);
  and and_7 (and_7_out, Op1, Bneg, Func5, Dneg);
  or or_2 (or_2_out, and_4_out, and_3_out, and_5_out);
  and and_8 (and_8_out, Aneg, Op0);
  and and_9 (and_9_out, and_6_out, or_1_out);
  and and_10 (and_10_out, Aneg, Bneg);
  and and_11 (and_11_out, and_7_out, or_2_out);
  or or_3 (out_9[2], and_8_out, and_9_out);
  or or_4 (out_9[0], and_10_out, and_11_out);
  and and_12 (and_12_out, Eneg, Fneg, Hneg);
  and and_13 (and_13_out, Fneg, Func1, Hneg);
  and and_14 (and_14_out, Op1, Bneg, Func5, Dneg);
  or or_5 (or_5_out, and_12_out, and_13_out);
  and and_15 (and_15_out, and_14_out, or_5_out);
  or or_6 (out_9[1], Aneg, and_15_out);

  // Other names for the same wires on the sheet: A = Op1; B = Op0; C = Func5; D = Func4; E = Func3; F = Func2;
  //   G = Func1; H = Func0; Z = out_9[0]; Y = out_9[1]; X = out_9[2]
endmodule

module MAIN_CONTROL (
  input  Op5,
  input  Op4,
  input  Op3,
  input  Op2,
  input  Op1,
  input  Op0,
  output Regdst,
  output ALUSrc,
  output MemtoReg,
  output RegWrite,
  output MemRead,
  output MemWrite,
  output Branch,
  output ALUOp1,
  output ALUOp0
);

  wire Aneg, Bneg, Cneg, Dneg, Eneg, Fneg;

  not not_1 (Aneg, Op5);
  not not_2 (Bneg, Op4);
  not not_3 (Cneg, Op3);
  not not_4 (Dneg, Op2);
  not not_5 (Eneg, Op1);
  not not_6 (Fneg, Op0);
  and and_1 (Regdst, Aneg, Bneg, Cneg, Dneg, Eneg, Fneg);
  and and_2 (ALUSrc, Op5, Bneg, Dneg, Op1, Op0);
  and and_3 (MemtoReg, Op5, Bneg, Cneg, Dneg, Op1, Op0);
  and and_4 (RegWrite, Cneg, Dneg);
  and and_5 (MemRead, Op5, Bneg, Cneg, Dneg, Op1, Op0);
  and and_6 (MemWrite, Op5, Bneg, Op3, Dneg, Op1, Op0);
  and and_7 (Branch, Aneg, Bneg, Cneg, Op2, Eneg, Fneg);
  and and_8 (ALUOp1, Aneg, Bneg, Cneg, Dneg, Eneg, Fneg);
  and and_9 (ALUOp0, Aneg, Bneg, Cneg, Op2, Eneg, Fneg);

  // Other names for the same wires on the sheet: A = Op5; B = Op4; C = Op3; D = Op2; E = Op1; F = Op0
endmodule
