// Logisim project lab2circuit.circ as structural Verilog: 9 circuits, main circuit main
module main (
);

  wire CLK, random_bit_generator_1_bit, RESET, S1, S2, S3;
  wire [6:0] visualization_1_c1_display_hundreds, visualization_1_c1_display_tens,
       visualization_1_c1_display_units, visualization_1_c2_display_hundreds,
       visualization_1_c2_display_tens, visualization_1_c2_display_units,
       visualization_1_c3_display_hundreds, visualization_1_c3_display_tens, visualization_1_c3_display_units;
  wire [7:0] event_counter_1_c1, event_counter_1_c2, event_counter_1_c3;

  Random_bit_generator random_bit_generator_1 (.RESET(RESET), .CLOCK(CLK), .BIT(random_bit_generator_1_bit));
  Event_Counter event_counter_1 (
    .S1(S1), .S2(S2), .S3(S3), .CLK(CLK), .RESET(RESET), .C1(event_counter_1_c1), .C2(event_counter_1_c2),
    .C3(event_counter_1_c3));
  BIt_secuence_detector bit_secuence_detector_1 (
    .X(random_bit_generator_1_bit), .CLK(CLK), .RESET(RESET), .S1(S1), .S2(S2), .S3(S3));
  Visualization visualization_1 (
    .C1(event_counter_1_c1), .C2(event_counter_1_c2), .C3(event_counter_1_c3),
    .C1_Display_Units(visualization_1_c1_display_units),
    .C1_Display_Hundreds(visualization_1_c1_display_hundreds),
    .C1_Display_Tens(visualization_1_c1_display_tens), .C2_Display_Units(visualization_1_c2_display_units),
    .C2_Display_Hundreds(visualization_1_c2_display_hundreds),
    .C2_Display_Tens(visualization_1_c2_display_tens), .C3_Display_Units(visualization_1_c3_display_units),
    .C3_Display_Hundreds(visualization_1_c3_display_hundreds),
    .C3_Display_Tens(visualization_1_c3_display_tens));
  Button button_1 (.out(RESET));
  Clock clock_1 (.out(CLK));
  _7_Segment_Display u_7_segment_display_1 (
    .g(visualization_1_c1_display_tens[6]), .f(visualization_1_c1_display_tens[5]),
    .a(visualization_1_c1_display_tens[0]), .b(visualization_1_c1_display_tens[1]),
    .e(visualization_1_c1_display_tens[4]), .d(visualization_1_c1_display_tens[3]),
    .c(visualization_1_c1_display_tens[2]));  // open: dp
  _7_Segment_Display u_7_segment_display_2 (
    .g(visualization_1_c2_display_tens[6]), .f(visualization_1_c2_display_tens[5]),
    .a(visualization_1_c2_display_tens[0]), .b(visualization_1_c2_display_tens[1]),
    .e(visualization_1_c2_display_tens[4]), .d(visualization_1_c2_display_tens[3]),
    .c(visualization_1_c2_display_tens[2]));  // open: dp
  _7_Segment_Display u_7_segment_display_3 (
    .g(visualization_1_c3_display_tens[6]), .f(visualization_1_c3_display_tens[5]),
    .a(visualization_1_c3_display_tens[0]), .b(visualization_1_c3_display_tens[1]),
    .e(visualization_1_c3_display_tens[4]), .d(visualization_1_c3_display_tens[3]),
    .c(visualization_1_c3_display_tens[2]));  // open: dp
  _7_Segment_Display u_7_segment_display_4 (
    .g(visualization_1_c1_display_hundreds[6]), .f(visualization_1_c1_display_hundreds[5]),
    .a(visualization_1_c1_display_hundreds[0]), .b(visualization_1_c1_display_hundreds[1]),
    .e(visualization_1_c1_display_hundreds[4]), .d(visualization_1_c1_display_hundreds[3]),
    .c(visualization_1_c1_display_hundreds[2]));  // open: dp
  _7_Segment_Display u_7_segment_display_5 (
    .g(visualization_1_c2_display_hundreds[6]), .f(visualization_1_c2_display_hundreds[5]),
    .a(visualization_1_c2_display_hundreds[0]), .b(visualization_1_c2_display_hundreds[1]),
    .e(visualization_1_c2_display_hundreds[4]), .d(visualization_1_c2_display_hundreds[3]),
    .c(visualization_1_c2_display_hundreds[2]));  // open: dp
  _7_Segment_Display u_7_segment_display_6 (
    .g(visualization_1_c3_display_hundreds[6]), .f(visualization_1_c3_display_hundreds[5]),
    .a(visualization_1_c3_display_hundreds[0]), .b(visualization_1_c3_display_hundreds[1]),
    .e(visualization_1_c3_display_hundreds[4]), .d(visualization_1_c3_display_hundreds[3]),
    .c(visualization_1_c3_display_hundreds[2]));  // open: dp
  _7_Segment_Display u_7_segment_display_7 (
    .g(visualization_1_c1_display_units[6]), .f(visualization_1_c1_display_units[5]),
    .a(visualization_1_c1_display_units[0]), .b(visualization_1_c1_display_units[1]),
    .e(visualization_1_c1_display_units[4]), .d(visualization_1_c1_display_units[3]),
    .c(visualization_1_c1_display_units[2]));  // open: dp
  _7_Segment_Display u_7_segment_display_8 (
    .g(visualization_1_c2_display_units[6]), .f(visualization_1_c2_display_units[5]),
    .a(visualization_1_c2_display_units[0]), .b(visualization_1_c2_display_units[1]),
    .e(visualization_1_c2_display_units[4]), .d(visualization_1_c2_display_units[3]),
    .c(visualization_1_c2_display_units[2]));  // open: dp
  _7_Segment_Display u_7_segment_display_9 (
    .g(visualization_1_c3_display_units[6]), .f(visualization_1_c3_display_units[5]),
    .a(visualization_1_c3_display_units[0]), .b(visualization_1_c3_display_units[1]),
    .e(visualization_1_c3_display_units[4]), .d(visualization_1_c3_display_units[3]),
    .c(visualization_1_c3_display_units[2]));  // open: dp
endmodule

module BCD2_7SEG_DECO (
  input  w,
  input  x,
  input  y,
  input  z,
  output a,
  output b,
  output c,
  output d,
  output e,
  output f,
  output g
);

  wire and_1_out, and_2_out, and_3_out, and_4_out, and_5_out, and_6_out, and_7_out, and_8_out, and_9_out,
       and_10_out, and_11_out, and_12_out, and_13_out, and_14_out, and_15_out, and_16_out, not_1_out,
       not_2_out, not_3_out, not_4_out;

  not not_1 (not_1_out, w);
  not not_2 (not_2_out, x);
  not not_3 (not_3_out, y);
  not not_4 (not_4_out, z);
  and and_1 (and_1_out, z, x);
  and and_2 (and_2_out, not_4_out, not_2_out);
  and and_3 (and_3_out, not_3_out, not_4_out);
  and and_4 (and_4_out, z, y);
  and and_5 (and_5_out, not_4_out, not_2_out);
  and and_6 (and_6_out, not_2_out, y);
  and and_7 (and_7_out, y, not_4_out);
  and and_8 (and_8_out, z, not_3_out, x);
  and and_9 (and_9_out, not_4_out, not_2_out);
  and and_10 (and_10_out, not_4_out, y);
  and and_11 (and_11_out, not_4_out, not_3_out);
  and and_12 (and_12_out, not_3_out, x);
  and and_13 (and_13_out, x, not_4_out);
  and and_14 (and_14_out, not_2_out, y);
  and and_15 (and_15_out, y, not_4_out);
  and and_16 (and_16_out, x, not_3_out);
  or or_1 (a, y, w, and_1_out, and_2_out);
  or or_2 (b, not_2_out, and_3_out, and_4_out);
  or or_3 (c, not_3_out, z, x);
  or or_4 (d, w, and_5_out, and_6_out, and_7_out, and_8_out);
  or or_5 (e, and_9_out, and_10_out);
  or or_6 (f, w, and_11_out, and_12_out, and_13_out);
  or or_7 (g, w, and_14_out, and_15_out, and_16_out);
endmodule

module Visualization_Cn (
  input  [7:0] C_n,
  output [6:0] display_unit,
  output [6:0] display_hundreds,
  output [6:0] display_tens
);

  wire [7:0] module_1_hundreds, module_1_tens, module_1_unit;

  Module module_1 (.C_n(C_n), .unit(module_1_unit), .hundreds(module_1_hundreds), .tens(module_1_tens));
  BCD2_7SEG_DECO bcd2_7seg_deco_1 (
    .w(module_1_unit[3]), .x(module_1_unit[2]), .y(module_1_unit[1]), .z(module_1_unit[0]),
    .a(display_unit[0]), .b(display_unit[1]), .c(display_unit[2]), .d(display_unit[3]), .e(display_unit[4]),
    .f(display_unit[5]), .g(display_unit[6]));
  BCD2_7SEG_DECO bcd2_7seg_deco_2 (
    .w(module_1_hundreds[3]), .x(module_1_hundreds[2]), .y(module_1_hundreds[1]), .z(module_1_hundreds[0]),
    .a(display_hundreds[0]), .b(display_hundreds[1]), .c(display_hundreds[2]), .d(display_hundreds[3]),
    .e(display_hundreds[4]), .f(display_hundreds[5]), .g(display_hundreds[6]));
  BCD2_7SEG_DECO bcd2_7seg_deco_3 (
    .w(module_1_tens[3]), .x(module_1_tens[2]), .y(module_1_tens[1]), .z(module_1_tens[0]),
    .a(display_tens[0]), .b(display_tens[1]), .c(display_tens[2]), .d(display_tens[3]), .e(display_tens[4]),
    .f(display_tens[5]), .g(display_tens[6]));
endmodule

module Module (
  input  [7:0] C_n,
  output [7:0] unit,
  output [7:0] hundreds,
  output [7:0] tens
);

  wire [7:0] divider_1_out;

  Divider divider_1 (.a(C_n), .b(8'ha), .out(divider_1_out), .rem(unit));  // open: upper
  Divider divider_2 (.a(divider_1_out), .b(8'ha), .out(tens), .rem(hundreds));  // open: upper
endmodule

module Event_Counter_Sn (
  input  CLK,
  input  Reset,
  output [7:0] C_n
);

  wire j_k_ff_1_qn, j_k_ff_2_qn, j_k_ff_3_qn, j_k_ff_4_qn, j_k_ff_5_qn, j_k_ff_6_qn, j_k_ff_7_qn;

  J_K_Flip_Flop j_k_ff_1 (.J(1'b1), .K(1'b1), .clk(CLK), .Q(C_n[0]), .Qn(j_k_ff_1_qn), .reset(Reset));  // open: preset
  J_K_Flip_Flop j_k_ff_2 (
    .J(1'b1), .K(1'b1), .clk(j_k_ff_1_qn), .Q(C_n[1]), .Qn(j_k_ff_2_qn), .reset(Reset));  // open: preset
  J_K_Flip_Flop j_k_ff_3 (
    .J(1'b1), .K(1'b1), .clk(j_k_ff_2_qn), .Q(C_n[2]), .Qn(j_k_ff_3_qn), .reset(Reset));  // open: preset
  J_K_Flip_Flop j_k_ff_4 (
    .J(1'b1), .K(1'b1), .clk(j_k_ff_3_qn), .Q(C_n[3]), .Qn(j_k_ff_4_qn), .reset(Reset));  // open: preset
  J_K_Flip_Flop j_k_ff_5 (
    .J(1'b1), .K(1'b1), .clk(j_k_ff_4_qn), .Q(C_n[4]), .Qn(j_k_ff_5_qn), .reset(Reset));  // open: preset
  J_K_Flip_Flop j_k_ff_6 (
    .J(1'b1), .K(1'b1), .clk(j_k_ff_5_qn), .Q(C_n[5]), .Qn(j_k_ff_6_qn), .reset(Reset));  // open: preset
  J_K_Flip_Flop j_k_ff_7 (
    .J(1'b1), .K(1'b1), .clk(j_k_ff_6_qn), .Q(C_n[6]), .Qn(j_k_ff_7_qn), .reset(Reset));  // open: preset
  J_K_Flip_Flop j_k_ff_8 (.J(1'b1), .K(1'b1), .clk(j_k_ff_7_qn), .Q(C_n[7]), .reset(Reset));  // open: Qn, preset
endmodule

module BIt_secuence_detector (
  input  X,
  input  CLK,
  input  RESET,
  output S1,
  output S2,
  output S3
);

  wire and_1_out, and_2_out, and_3_out, and_4_out, and_5_out, and_6_out, and_7_out, and_8_out, and_9_out,
       and_10_out, and_11_out, and_12_out, and_13_out, and_14_out, and_15_out, and_16_out, and_17_out,
       and_18_out, and_19_out, and_20_out, and_21_out, and_22_out, and_23_out, J0, J1, J2, J3, K0, K1, K2,
       K3, Q0, Q0not, Q1, Q1not, Q2, Q2not, Q3, Q3not, Xnot;

  not not_1 (Xnot, X);
  and and_1 (and_1_out, Q1, Q2, Q0not);
  and and_2 (and_2_out, Q2, X, Q1);
  and and_3 (and_3_out, Q2, Q1not, Q0, Xnot);
  and and_4 (and_4_out, Q1not, Q0not);
  and and_5 (and_5_out, Q1not, X);
  and and_6 (and_6_out, Q1, Q0);
  and and_7 (and_7_out, Q3not, Q1);
  and and_8 (and_8_out, Q1, Q0, X);
  and and_9 (and_9_out, Q3, Q1not, X);
  and and_10 (and_10_out, Q1not, Xnot);
  and and_11 (and_11_out, Q0not, Xnot);
  and and_12 (and_12_out, Q1, X);
  or or_1 (J3, and_1_out, and_2_out, and_3_out);
  or or_2 (J2, and_7_out, and_8_out, and_9_out);
  or or_3 (K2, and_10_out, and_11_out, and_12_out);
  or or_4 (K3, and_4_out, and_5_out, and_6_out);
  and and_13 (and_13_out, Q0not, X);
  and and_14 (and_14_out, Q3not, Q2not, X);
  and and_15 (and_15_out, Q3, Q0, Xnot);
  and and_16 (and_16_out, Q1not, Xnot);
  and and_17 (and_17_out, Q1, X);
  and and_18 (and_18_out, Q2, Q1not);
  and and_19 (and_19_out, Q3, Q1not);
  and and_20 (and_20_out, Q3not, Q1);
  and and_21 (and_21_out, Q2, Xnot);
  or or_5 (K1, Q0not, Xnot);
  or or_6 (J1, and_13_out, and_14_out, and_15_out);
  or or_7 (J0, and_16_out, and_17_out, and_18_out, and_19_out);
  or or_8 (K0, and_20_out, and_21_out);
  J_K_Flip_Flop j_k_ff_1 (.J(J3), .K(K3), .clk(CLK), .Q(Q3), .Qn(Q3not), .reset(RESET));  // open: preset
  J_K_Flip_Flop j_k_ff_2 (.J(J2), .K(K2), .clk(CLK), .Q(Q2), .Qn(Q2not), .reset(RESET));  // open: preset
  J_K_Flip_Flop j_k_ff_3 (.J(J1), .K(K1), .clk(CLK), .Q(Q1), .Qn(Q1not), .reset(RESET));  // open: preset
  J_K_Flip_Flop j_k_ff_4 (.J(J0), .K(K0), .clk(CLK), .Q(Q0), .Qn(Q0not), .reset(RESET));  // open: preset
  and and_22 (and_22_out, Q3, Q1not, Q0not);
  and and_23 (and_23_out, Q3, Q1, Q0);
  and and_24 (S2, Q3, Q1, Q0not);
  and and_25 (S3, Q3, Q1, Q0);
  or or_9 (S1, and_22_out, and_23_out);

  // Other names for the same wires on the sheet: CLR = RESET
endmodule

module Random_bit_generator (
  input  RESET,
  input  CLOCK,
  output BIT
);

  Random #(.width(1)) random_1 (.clr(RESET), .clk(CLOCK), .out(BIT));  // open: next
endmodule

module Event_Counter (
  input  S1,
  input  S2,
  input  S3,
  input  CLK,
  input  RESET,
  output [7:0] C1,
  output [7:0] C2,
  output [7:0] C3
);

  wire and_1_out, and_2_out, and_3_out, not_1_out, not_2_out, not_3_out;

  not not_1 (not_1_out, CLK);
  not not_2 (not_2_out, CLK);
  not not_3 (not_3_out, CLK);
  and and_1 (and_1_out, not_1_out, S1);
  and and_2 (and_2_out, not_2_out, S2);
  and and_3 (and_3_out, not_3_out, S3);
  Event_Counter_Sn event_counter_sn_1 (.CLK(and_1_out), .Reset(RESET), .C_n(C1));
  Event_Counter_Sn event_counter_sn_2 (.CLK(and_2_out), .Reset(RESET), .C_n(C2));
  Event_Counter_Sn event_counter_sn_3 (.CLK(and_3_out), .Reset(RESET), .C_n(C3));
endmodule

module Visualization (
  input  [7:0] C1,
  input  [7:0] C2,
  input  [7:0] C3,
  output [6:0] C1_Display_Units,
  output [6:0] C1_Display_Hundreds,
  output [6:0] C1_Display_Tens,
  output [6:0] C2_Display_Units,
  output [6:0] C2_Display_Hundreds,
  output [6:0] C2_Display_Tens,
  output [6:0] C3_Display_Units,
  output [6:0] C3_Display_Hundreds,
  output [6:0] C3_Display_Tens
);

  Visualization_Cn visualization_cn_1 (
    .C_n(C1), .display_unit(C1_Display_Units), .display_hundreds(C1_Display_Hundreds),
    .display_tens(C1_Display_Tens));
  Visualization_Cn visualization_cn_2 (
    .C_n(C2), .display_unit(C2_Display_Units), .display_hundreds(C2_Display_Hundreds),
    .display_tens(C2_Display_Tens));
  Visualization_Cn visualization_cn_3 (
    .C_n(C3), .display_unit(C3_Display_Units), .display_hundreds(C3_Display_Hundreds),
    .display_tens(C3_Display_Tens));
endmodule
